# Fritzing sketch OYS_ODEV_CIZIM (saved by Fritzing 0.9.4)

parts:
  U2 = ESP32S-HiLetgo [part_number=ESP32S-HiLetgo]
  OLED_I2C1 = OLED 128x64 I2C Monochrome Display
  Parça2 = RFID-RC522-v3

nets:
  N1: U2.GPIO11, OLED_I2C1.GND
  VIN: U2.VIN, OLED_I2C1.VDD
  N2: U2.GPIO6, Parça2.3.3V
  N3: U2.GPIO7, Parça2.GND
  N4: U2.GPIO2, Parça2.RST
  N5: U2.GPIO16, Parça2.SDA
  N6: U2.GPIO17, Parça2.SCK
  N7: U2.GPIO5, Parça2.MISO
  N8: U2.GPIO18, OLED_I2C1.SDA
  N9: U2.GPIO23, OLED_I2C1.SCK
  N10: U2.GND, Parça2.MOSI

custom parts:
  ESP32S-HiLetgo: HiLetgo ESP-WROOM-32 ESP32 ESP-32S Development Board 2.4GHz Dual-Mode WiFi + Bluetooth Dual Cores Microcontroller The ESP32 integrated with Antenna switches, RF Balun, power amplifiers, low-noise amplifiers, filters, and management modules, and the entire solution occupies the least area of PCB. 2.4 GHz Wi-Fi plus Bluetooth dual-mode chip, with TSMC Ultra-low power consumption 40nm technology,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
  RFID-RC522-v3: A simple China made RFID-RC522 Reader (6x4 cm); do check the pin labels, as this is a MFRC522 based clone.
